# Fritzing sketch matrix (saved by Fritzing 0.9.3b)

parts:
  元件1 = Arduino Uno (Rev3)
  Disp1 = LBT2088AH [part_number=LBT2088AH]

nets:
  N1: 元件1.A0, Disp1.pin_6
  N2: 元件1.A1, Disp1.pin_11
  N3: 元件1.A2, Disp1.pin_15
  N4: 元件1.A3, Disp1.pin_16
  N5: 元件1.D8, Disp1.pin2
  N6: 元件1.D9_PWM, Disp1.pin_5
  N7: 元件1.D10_PWM/SS, Disp1.pin_13
  N8: 元件1.D11_PWM/MOSI, Disp1.pin_3
  N9: 元件1.D12/MISO, Disp1.pin_4
  N10: 元件1.D13/SCK, Disp1.pin_10
  N11: 元件1.D2, Disp1.pin_9
  N12: 元件1.D3_PWM, Disp1.pin_14
  N13: 元件1.D4, Disp1.pin_8
  N14: 元件1.D5_PWM, Disp1.pin_12
  N15: 元件1.D6_PWM, Disp1.pin1
  N16: 元件1.D7, Disp1.pin_7
