# Fritzing sketch matrix_V2 (saved by Fritzing 0.9.3b)
breadboards: 1

parts:
  元件1 = Arduino Uno (Rev3)
  Disp1 = LBT2088AH [part_number=LBT2088AH]
  U3 = 74HC595 SMD [package="SO16 [SMD]"]
  U4 = 74HC595 SMD [package="SO16 [SMD]"]

nets:
  N1: 元件1.D2, U4.DS
  N2: 元件1.D3_PWM, U4.SH_CP
  N3: 元件1.D4, U4.ST_CP
  N4: 元件1.D5_PWM, U3.DS
  N5: 元件1.D6_PWM, U3.SH_CP
  5V: 元件1.5V, U3.MR, U4.VCC
  GND: 元件1.GND, U4.GND, U4.OE
  N6: Disp1.pin1, U4.Q4
  N7: Disp1.pin2, U4.Q6
  N8: Disp1.pin_3, U3.Q1
  N9: Disp1.pin_4, U3.Q2
  N10: Disp1.pin_5, U4.Q7
  N11: Disp1.pin_6, U3.Q4
  N12: Disp1.pin_7, U4.Q5
  N13: Disp1.pin_8, U4.Q2
  N14: Disp1.pin_9, U4.Q0
  N15: Disp1.pin_10, U3.Q3
  N16: Disp1.pin_11, U3.Q5
  N17: Disp1.pin_12, U4.Q3
  N18: Disp1.pin_13, U3.Q0
  N19: Disp1.pin_14, U4.Q1
  N20: Disp1.pin_15, U3.Q6
  N21: Disp1.pin_16, U3.Q7
  N22: U3.GND, U3.OE
